# Fritzing sketch CD4067 + Arduino Pro Micro_schematic (saved by Fritzing 0.9.3b)
breadboards: 1

parts:
  Pro_Micro2 = Pro Micro  # not connected
  HCF_2 = HCF 4067 [package="DIP24 [THT]"]

nets:
  N1: HCF_2.12_VSS, HCF_2.15_Inhibit

custom parts:
  Pro Micro: The SparkFun Pro Micro is a complete USB-based microcontoller development system, in a very small footprint, capable of implementing many types of projects. All programming can be done via the USB port.
