# Fritzing sketch Fliper DJ (clean)_schematic (saved by Fritzing 0.9.3b)
breadboards: 1

parts:
  Pro_Micro3 = Pro Micro  # not connected
  HCF_3 = HCF 4067 [package="DIP24 [THT]"]
  BUTTON2 = Arcade Button (green)
  BUTTON3 = Arcade Button (green)
  BUTTON4 = Arcade Button (green)
  BUTTON5 = Arcade Button (green)
  BUTTON6 = Arcade Button (blue)
  BUTTON7 = Arcade Button (blue)
  BUTTON8 = Arcade Button (blue)
  BUTTON9 = Arcade Button (blue)
  BUTTON10 = Arcade Button (blue)
  BUTTON11 = Arcade Button (blue)
  BUTTON12 = Arcade Button (green)
  BUTTON13 = Arcade Button (green)
  BUTTON14 = Arcade Button (blue)
  BUTTON15 = Arcade Button (blue)
  BUTTON16 = Arcade Button (green)
  BUTTON17 = Arcade Button (green)
  R1 = Rotary Potentiometer (Small) [maximum_resistance=100kΩ package=THT]
  R2 = Rotary Potentiometer (Small) [maximum_resistance=100kΩ package=THT]
  R3 = Rotary Potentiometer (Small) [maximum_resistance=100kΩ package=THT]
  R4 = Rotary Potentiometer (Small) [maximum_resistance=100kΩ package=THT]
  R5 = Rotary Potentiometer (Small) [maximum_resistance=100kΩ package=THT]
  R6 = Rotary Potentiometer (Small) [maximum_resistance=100kΩ package=THT]
  R7 = Rotary Potentiometer (Small) [maximum_resistance=100kΩ package=THT]
  R8 = Slide Potentiometer [maximum_resistance=100kΩ]
  R9 = Slide Potentiometer [maximum_resistance=100kΩ]
  U1 = SLIDER [package=slider]

nets:
  N1: HCF_3.12_VSS, HCF_3.15_Inhibit
  N2: BUTTON2.no_name_yet, BUTTON3.no_name_yet, BUTTON4.no_name_yet, BUTTON5.no_name_yet, BUTTON6.no_name_yet, BUTTON7.no_name_yet, BUTTON8.no_name_yet, BUTTON9.no_name_yet, BUTTON10.no_name_yet, BUTTON11.no_name_yet, BUTTON12.no_name_yet, BUTTON13.no_name_yet, BUTTON14.no_name_yet, BUTTON15.no_name_yet, BUTTON16.no_name_yet, BUTTON17.no_name_yet, R1.leg2, R2.leg2, R3.leg2, R4.leg2, R5.leg2, R6.leg2, R7.leg2, R9.leg2, U1.A
  N3: R1.leg1, R2.leg1, R3.leg1, R4.leg1, R5.leg1, R6.leg1, R7.leg1, R8.leg1, R9.leg1, U1.E

custom parts:
  Pro Micro: The SparkFun Pro Micro is a complete USB-based microcontoller development system, in a very small footprint, capable of implementing many types of projects. All programming can be done via the USB port.
  Arcade Button (green): Adafruit Arcade Button (green)
  Arcade Button (blue): Adafruit Arcade Button (blue)
