# Fritzing sketch Fliper DJ_schematic (saved by Fritzing 0.9.3b)
breadboards: 1

parts:
  Pro_Micro3 = Pro Micro  # not connected
  HCF_3 = HCF 4067 [package="DIP24 [THT]"]
  BUTTON2 = Arcade Button (green)
  BUTTON3 = Arcade Button (green)
  BUTTON4 = Arcade Button (green)
  BUTTON5 = Arcade Button (green)
  BUTTON6 = Arcade Button (blue)
  BUTTON7 = Arcade Button (blue)
  BUTTON8 = Arcade Button (blue)
  BUTTON9 = Arcade Button (blue)
  BUTTON10 = Arcade Button (blue)
  BUTTON11 = Arcade Button (blue)
  BUTTON12 = Arcade Button (green)
  BUTTON13 = Arcade Button (green)
  BUTTON14 = Arcade Button (blue)
  BUTTON15 = Arcade Button (blue)
  BUTTON16 = Arcade Button (green)
  BUTTON17 = Arcade Button (green)
  R1 = Rotary Potentiometer (Small) [maximum_resistance=100kΩ package=THT]
  R2 = Rotary Potentiometer (Small) [maximum_resistance=100kΩ package=THT]
  R3 = Rotary Potentiometer (Small) [maximum_resistance=100kΩ package=THT]
  R4 = Rotary Potentiometer (Small) [maximum_resistance=100kΩ package=THT]
  R5 = Rotary Potentiometer (Small) [maximum_resistance=100kΩ package=THT]
  R6 = Rotary Potentiometer (Small) [maximum_resistance=100kΩ package=THT]
  R7 = Rotary Potentiometer (Small) [maximum_resistance=100kΩ package=THT]
  R8 = Slide Potentiometer [maximum_resistance=100kΩ]
  R9 = Slide Potentiometer [maximum_resistance=100kΩ]
  U1 = SLIDER [package=slider]

nets:
  N1: HCF_3.3_TG6, R7.wiper
  N2: HCF_3.4_TG5, R2.wiper
  N3: HCF_3.5_TG4, R1.wiper
  N4: HCF_3.6_TG3, R4.wiper
  N5: HCF_3.7_TG2, R3.wiper
  N6: HCF_3.8_TG1, R6.wiper
  N7: HCF_3.9_TG0, R5.wiper
  N8: HCF_3.12_VSS, HCF_3.15_Inhibit, BUTTON2.no_name_yet#1, BUTTON3.no_name_yet#1, BUTTON4.no_name_yet#1, BUTTON5.no_name_yet#1, BUTTON6.no_name_yet#1, BUTTON7.no_name_yet#1, BUTTON8.no_name_yet#1, BUTTON9.no_name_yet#1, BUTTON10.no_name_yet#1, BUTTON11.no_name_yet#1, BUTTON12.no_name_yet#1, BUTTON13.no_name_yet#1, BUTTON14.no_name_yet#1, BUTTON15.no_name_yet#1, BUTTON16.no_name_yet#1, BUTTON17.no_name_yet#1, R1.leg2, R2.leg2, R3.leg2, R4.leg2, R5.leg2, R6.leg2, R7.leg2, R8.leg2, R9.leg2, U1.A
  N9: HCF_3.16_TG15, BUTTON11.no_name_yet#2
  N10: HCF_3.17_TG14, BUTTON15.no_name_yet#2
  N11: HCF_3.18_TG13, BUTTON10.no_name_yet#2
  N12: HCF_3.19_TG12, BUTTON14.no_name_yet#2
  N13: HCF_3.20_TG11, BUTTON16.no_name_yet#2
  N14: HCF_3.21_TG10, U1.S
  N15: HCF_3.22_TG9, R9.wiper
  N16: HCF_3.23_TG8, R8.wiper
  N17: HCF_3.24_Vdd, R1.leg1, R2.leg1, R3.leg1, R4.leg1, R5.leg1, R6.leg1, R7.leg1, R8.leg1, R9.leg1, U1.E

notes:
  DIY MIDI Controller
  by Gustavo Silveira
  www.musiconerd.com
  gustavosilveira@musiconerd.com
  Arduino Pro Micro + Multiplexer 4067
  Slide potentiometers pins
  1 = gnd
  2 = wiper
  3 = 5v

custom parts:
  Pro Micro: The SparkFun Pro Micro is a complete USB-based microcontoller development system, in a very small footprint, capable of implementing many types of projects. All programming can be done via the USB port.
  Arcade Button (green): Adafruit Arcade Button (green)
  Arcade Button (blue): Adafruit Arcade Button (blue)
